// Logisim project additionneur.circ as structural Verilog: 3 circuits, main circuit main
module main (
  input  [3:0] in_1,
  input  [3:0] in_2,
  output [3:0] out_3,
  output out_4
);

  wire and_1_out, bit_complet_2_out_5, bit_complet_3_out_5, bit_complet_out_5, not_1_out;

  not not_1 (not_1_out, in_1[0]);
  and and_1 (and_1_out, not_1_out, in_1[0]);
  \bite_complète  bit_complet (
    .in_1(and_1_out), .in_2(in_1[0]), .in_3(in_2[0]), .out_4(out_3[0]), .out_5(bit_complet_out_5));
  \bite_complète  bit_complet_2 (
    .in_1(bit_complet_out_5), .in_2(in_1[1]), .in_3(in_2[1]), .out_4(out_3[1]), .out_5(bit_complet_2_out_5));
  \bite_complète  bit_complet_3 (
    .in_1(bit_complet_2_out_5), .in_2(in_1[2]), .in_3(in_2[2]), .out_4(out_3[2]), .out_5(bit_complet_3_out_5));
  \bite_complète  bit_complet_4 (
    .in_1(bit_complet_3_out_5), .in_2(in_1[3]), .in_3(in_2[3]), .out_4(out_3[3]), .out_5(out_4));
endmodule

module demi_bite (
  input  in_1,
  input  in_2,
  output out_3,
  output out_4
);

  xor xor_1 (out_3, in_1, in_2);
  and and_1 (out_4, in_1, in_2);
endmodule

module \bite_complète  (
  input  in_1,
  input  in_2,
  input  in_3,
  output out_4,
  output out_5
);

  wire demi_bit_2_out_4, demi_bit_out_3, demi_bit_out_4;

  demi_bite demi_bit (.in_1(in_1), .in_2(in_2), .out_3(demi_bit_out_3), .out_4(demi_bit_out_4));
  demi_bite demi_bit_2 (.in_1(demi_bit_out_3), .in_2(in_3), .out_3(out_4), .out_4(demi_bit_2_out_4));
  or or_1 (out_5, demi_bit_2_out_4, demi_bit_out_4);
endmodule
