// Logisim project projet_archi_dufillon_croquefer.circ as structural Verilog: 4 circuits, main circuit main
module main (
  input  in_1,
  input  in_2,
  input  in_3
);

  wire button_1_out, clock_1_out, clock_2_out, counter_1_carry, decoder_1_out0, decoder_1_out1,
       decoder_1_out2, decoder_1_out3, decoder_1_out4, decoder_1_out5, multiplexer_1_out, nand_1_out,
       not_1_out, not_2_out, not_3_out, not_4_out, or_1_out, or_3_out, or_4_out;
  wire [1:0] controlled_buffer_1_out, rom_1_data, rom_1_data_2, rom_1_data_3, rom_1_data_5;
  wire [2:0] bitselector_1_out;
  wire [7:0] bancregistre_1_out_7, bitselector_2_out, counter_1_q, demultiplexer_1_out0,
       demultiplexer_1_out1, multiplexer_2_out, register_1_q, register_2_q, unitecalcul_1_out_5;
  wire [15:2] rom_1_data_4;

  Clock #(.highDuration(10)) clock_1 (.out(clock_1_out));
  Counter counter_1 (
    .Q(counter_1_q), .carry(counter_1_carry), .clk(clock_1_out), .clr(button_1_out));  // open: load, D, count
  Button button_1 (.out(button_1_out));
  not not_1 (not_1_out, counter_1_carry);
  ROM #(.dataWidth(16)) rom_1 (
    .addr(counter_1_q),
    .data({rom_1_data_4[15:9], rom_1_data, rom_1_data_3, rom_1_data_2, rom_1_data_4[2], rom_1_data_5}),
    .sel(not_1_out));
  Decoder #(.select(3), .enable("false")) decoder_1 (
    .out0(decoder_1_out0), .out1(decoder_1_out1), .out2(decoder_1_out2), .out3(decoder_1_out3),
    .out4(decoder_1_out4), .out5(decoder_1_out5), .sel(bitselector_1_out));  // open: out6, out7
  BitSelector #(.width(16), .group(3)) bitselector_1 (
    .in({rom_1_data_4[15:9], rom_1_data, rom_1_data_3, rom_1_data_2, rom_1_data_4[2], rom_1_data_5}),
    .out(bitselector_1_out), .sel(3'b000));
  assign controlled_buffer_1_out = or_1_out ? rom_1_data : 2'bz;  // Controlled_Buffer controlled_buffer_1
  BitSelector #(.width(16), .group(8)) bitselector_2 (
    .in({rom_1_data_4[15:9], rom_1_data, rom_1_data_3, rom_1_data_2, rom_1_data_4[2], rom_1_data_5}),
    .out(bitselector_2_out), .sel(1'b1));
  assign controlled_buffer_1_out = multiplexer_1_out ? rom_1_data_3 : 2'bz;  // Controlled_Buffer controlled_buffer_2
  Multiplexer #(.enable("false")) multiplexer_1 (
    .in0(or_1_out), .in1(not_2_out), .out(multiplexer_1_out), .sel(or_1_out));
  not not_2 (not_2_out, or_1_out);
  assign controlled_buffer_1_out = not_3_out ? rom_1_data_2 : 2'bz;  // Controlled_Buffer controlled_buffer_3
  not not_3 (not_3_out, or_1_out);
  or or_1 (or_1_out, register_1_q[0], register_1_q[1], register_1_q[2], register_1_q[3], register_1_q[4], register_1_q[5], register_1_q[6], register_1_q[7]);
  or or_2 (or_1_out, register_2_q[0], register_2_q[1], register_2_q[2], register_2_q[3], register_2_q[4], register_2_q[5], register_2_q[6], register_2_q[7]);
  LED ADD (.in(decoder_1_out0));
  LED SUB (.in(decoder_1_out1));
  LED DIV (.in(decoder_1_out2));
  LED MUL (.in(decoder_1_out3));
  LED LOAD (.in(decoder_1_out4));
  LED END (.in(decoder_1_out5));
  Multiplexer #(.width(8), .enable("false")) multiplexer_2 (
    .in0(unitecalcul_1_out_5), .in1(bitselector_2_out), .out(multiplexer_2_out), .sel(decoder_1_out4));
  or or_3 (or_3_out, decoder_1_out3, decoder_1_out2, decoder_1_out1, decoder_1_out0);
  Demultiplexer #(.width(8), .enable("false")) demultiplexer_1 (
    .out0(demultiplexer_1_out0), .out1(demultiplexer_1_out1), .in(bancregistre_1_out_7), .sel(or_1_out));
  Clock clock_2 (.out(clock_2_out));
  Register register_1 (
    .D(demultiplexer_1_out0), .en(not_4_out), .Q(register_1_q), .clk(clock_2_out), .clr(clock_1_out));
  nand nand_1 (nand_1_out, or_1_out, or_4_out);
  not not_4 (not_4_out, or_1_out);
  or or_4 (or_4_out, decoder_1_out4, or_1_out);
  Register register_2 (
    .D(demultiplexer_1_out1), .en(nand_1_out), .Q(register_2_q), .clk(clock_2_out), .clr(clock_1_out));
  bancregistre bancregistre_1 (
    .in_3(multiplexer_2_out), .in_4(clock_2_out), .in_5(in_2), .in_6(controlled_buffer_1_out),
    .out_7(bancregistre_1_out_7), .in_1(in_1), .in_2(in_3));
  unitecalcul unitecalcul_1 (
    .in_1(register_1_q), .in_2(register_2_q), .in_3(rom_1_data_5), .in_4(or_3_out),
    .out_5(unitecalcul_1_out_5));
  // Probe on unitecalcul_1_out_5
  // Probe on bancregistre_1_out_7

  // Notes on the sheet:
  //   contents of rom_1 (hex, n*v repeats v):
  //   c04 e70c 1114 1c1 5b 41 5
endmodule

module inverseur (
  input  [7:0] in_1,
  output [7:0] out_2
);

  wire bitselector_1_out;
  wire [7:0] negator_1_out;

  BitSelector bitselector_1 (.in(in_1), .out(bitselector_1_out), .sel(3'b111));
  Negator negator_1 (.in(in_1), .out(negator_1_out));
  Multiplexer #(.width(8), .enable("false")) multiplexer_1 (
    .in0(in_1), .in1(negator_1_out), .out(out_2), .sel(bitselector_1_out));
endmodule

module unitecalcul (
  input  [7:0] in_1,
  input  [7:0] in_2,
  input  [1:0] in_3,
  input  in_4,
  output [7:0] out_5
);

  wire bitselector_1_out, bitselector_2_out, xor_1_out;
  wire [7:0] adder_1_out, adder_2_out, divider_1_out, inverseur_1_out_2, inverseur_2_out_2,
       multiplexer_1_out, multiplexer_2_out, multiplexer_3_out, multiplier_1_out, negator_1_out,
       negator_2_out, negator_3_out;

  BitSelector bitselector_1 (.in(in_1), .out(bitselector_1_out), .sel(3'b111));
  BitSelector bitselector_2 (.in(in_2), .out(bitselector_2_out), .sel(3'b111));
  inverseur inverseur_1 (.in_1(in_1), .out_2(inverseur_1_out_2));
  inverseur inverseur_2 (.in_1(in_2), .out_2(inverseur_2_out_2));
  xor xor_1 (xor_1_out, bitselector_1_out, bitselector_2_out);
  Negator negator_1 (.in(in_2), .out(negator_1_out));
  Multiplier multiplier_1 (.a(inverseur_1_out_2), .b(inverseur_2_out_2), .out(multiplier_1_out));  // open: cin, cout
  Divider divider_1 (.a(inverseur_1_out_2), .b(inverseur_2_out_2), .out(divider_1_out));  // open: upper, rem
  Adder adder_1 (.a(in_1), .b(in_2), .out(adder_1_out));  // open: cin, cout
  Adder adder_2 (.a(in_1), .b(negator_1_out), .out(adder_2_out));  // open: cin, cout
  Negator negator_2 (.in(multiplier_1_out), .out(negator_2_out));
  Multiplexer #(.width(8), .enable("false")) multiplexer_1 (
    .in0(divider_1_out), .in1(negator_3_out), .out(multiplexer_1_out), .sel(xor_1_out));
  Negator negator_3 (.in(divider_1_out), .out(negator_3_out));
  Multiplexer #(.width(8), .enable("false")) multiplexer_2 (
    .in0(multiplier_1_out), .in1(negator_2_out), .out(multiplexer_2_out), .sel(xor_1_out));
  Multiplexer #(.select(2), .width(8), .enable("false")) multiplexer_3 (
    .in0(adder_1_out), .in1(adder_2_out), .in2(multiplexer_2_out), .in3(multiplexer_1_out),
    .out(multiplexer_3_out), .sel(in_3));
  assign out_5 = in_4 ? multiplexer_3_out : 8'bz;  // Controlled_Buffer controlled_buffer_1
endmodule

module bancregistre (
  input  in_1,
  input  in_2,
  input  [7:0] in_3,
  input  in_4,
  input  in_5,
  input  [1:0] in_6,
  output [7:0] out_7
);

  wire and_1_out, and_2_out, and_3_out, and_4_out, decoder_1_out0, decoder_1_out1, decoder_1_out2,
       decoder_1_out3;
  wire [7:0] multiplexer_1_out, multiplexer_2_out, multiplexer_3_out, multiplexer_4_out, register_1_q,
       register_2_q, register_3_q, register_4_q;

  Multiplexer #(.width(8), .enable("false")) multiplexer_1 (
    .in0(register_1_q), .in1(in_3), .out(multiplexer_1_out), .sel(and_1_out));
  and and_1 (and_1_out, in_1, in_2, decoder_1_out0);
  Register register_1 (.D(multiplexer_1_out), .Q(register_1_q), .clk(in_4));  // open: en, clr
  Multiplexer #(.width(8), .enable("false")) multiplexer_2 (
    .in0(register_2_q), .in1(in_3), .out(multiplexer_2_out), .sel(and_2_out));
  Register register_2 (.D(multiplexer_2_out), .Q(register_2_q), .clk(in_4));  // open: en, clr
  and and_2 (and_2_out, in_1, in_2, decoder_1_out1);
  Decoder #(.select(2)) decoder_1 (
    .out0(decoder_1_out0), .out1(decoder_1_out1), .out2(decoder_1_out2), .out3(decoder_1_out3), .sel(in_6),
    .en(in_5));
  and and_3 (and_3_out, in_1, in_2, decoder_1_out2);
  Multiplexer #(.width(8), .enable("false")) multiplexer_3 (
    .in0(register_3_q), .in1(in_3), .out(multiplexer_3_out), .sel(and_3_out));
  Register register_3 (.D(multiplexer_3_out), .Q(register_3_q), .clk(in_4));  // open: en, clr
  Multiplexer #(.width(8), .enable("false")) multiplexer_4 (
    .in0(register_4_q), .in1(in_3), .out(multiplexer_4_out), .sel(and_4_out));
  and and_4 (and_4_out, in_1, in_2, decoder_1_out3);
  Register register_4 (.D(multiplexer_4_out), .Q(register_4_q), .clk(in_4));  // open: en, clr
  Multiplexer #(.select(2), .width(8)) multiplexer_5 (
    .in0(register_1_q), .in1(register_2_q), .in2(register_3_q), .in3(register_4_q), .out(out_7), .sel(in_6),
    .en(1'b1));
endmodule
