// Logisim project comparateur_binaire.circ as structural Verilog: 1 circuit, main circuit main
module main (
  input  a,
  input  in_2
);

  wire and_1_out, and_2_out, and_3_out, and_4_out, not_1_out, not_2_out, or_1_p4, undriven;

  not not_1 (not_1_out, a);
  not not_2 (not_2_out, in_2);
  and and_1 (and_1_out, a, not_2_out, undriven);
  and and_2 (and_2_out, undriven, not_1_out, in_2);
  and and_3 (and_3_out, a, in_2);
  and and_4 (and_4_out, not_2_out, not_1_out);
  // OR_Gate or_1: pin names not known; wires that end beside it: and_3_out, and_3_out, and_4_out, or_1_p4
  LED led_1 (.in(and_1_out));
  LED led_2 (.in(and_2_out));
  LED led_3 (.in(or_1_p4));

  // Notes on the sheet:
  //   a>b
  //   a<b
  //   a=b
endmodule
