// Logisim project Projet_Architecture_des_Ordinateurs.circ as structural Verilog: 3 circuits, main circuit main
module main (
  input  in_1,
  input  in_2,
  input  in_3,
  input  in_4
);

  wire button_1_out, clock_1_out, clock_2_out, comparator_1_eq, controlled_buffer_1_out, decoder_1_out0,
       decoder_1_out1, decoder_1_out2, decoder_1_out3, decoder_1_out4, decoder_1_out5, multiplexer_1_out,
       nand_1_p2, nand_1_p3, not_1_out, not_2_out, not_3_out, or_1_out, or_2_out, or_3_out;
  wire [1:0] controlled_buffer_3_out;
  wire [2:0] bitselector_1_out;
  wire [7:0] banc_de_registre_1_out_7, bitselector_2_out, counter_1_q, demultiplexer_1_out0,
       demultiplexer_1_out1, multiplexer_2_out, register_1_q, register_2_q, \unité_de_calcul_1_out_5 ;
  wire [15:0] rom_1_data;

  Clock #(.highDuration(10)) clock_1 (.out(clock_1_out));
  Counter counter_1 (.Q(counter_1_q), .clk(clock_1_out), .clr(controlled_buffer_1_out));  // open: load, D, count, carry
  assign controlled_buffer_1_out = button_1_out ? comparator_1_eq : 1'bz;  // Controlled_Buffer controlled_buffer_1
  Button button_1 (.out(button_1_out));
  assign controlled_buffer_1_out = comparator_1_eq ? 1'b1 : 1'bz;  // Controlled_Buffer controlled_buffer_2
  ROM #(.dataWidth(16)) rom_1 (.addr(counter_1_q), .data(rom_1_data));  // open: sel
  Comparator #(.width(16)) comparator_1 (.a(rom_1_data), .b({16{1'b0}}), .eq(comparator_1_eq));  // open: gt, lt
  Decoder #(.select(3)) decoder_1 (
    .out0(decoder_1_out0), .out1(decoder_1_out1), .out2(decoder_1_out2), .out3(decoder_1_out3),
    .out4(decoder_1_out4), .out5(decoder_1_out5), .sel(bitselector_1_out));  // open: out6, out7, en
  BitSelector #(.width(16), .group(3)) bitselector_1 (.in(rom_1_data), .out(bitselector_1_out), .sel(3'b000));
  BitSelector #(.width(16), .group(8)) bitselector_2 (.in(rom_1_data), .out(bitselector_2_out), .sel(1'b1));
  assign controlled_buffer_3_out = or_3_out ? rom_1_data[8:7] : 2'bz;  // Controlled_Buffer controlled_buffer_3
  LED ADD (.in(decoder_1_out0));
  LED SUB (.in(decoder_1_out1));
  LED DIV (.in(decoder_1_out2));
  LED MUL (.in(decoder_1_out3));
  LED LOAD (.in(decoder_1_out4));
  LED END (.in(decoder_1_out5));
  assign controlled_buffer_3_out = multiplexer_1_out ? rom_1_data[6:5] : 2'bz;  // Controlled_Buffer controlled_buffer_4
  Multiplexer #(.enable("false")) multiplexer_1 (
    .in0(or_2_out), .in1(not_1_out), .out(multiplexer_1_out), .sel(or_3_out));
  not not_1 (not_1_out, or_2_out);
  or or_1 (or_1_out, decoder_1_out3, decoder_1_out2, decoder_1_out1, decoder_1_out0);
  not not_2 (not_2_out, or_2_out);
  Clock clock_2 (.out(clock_2_out));
  assign controlled_buffer_3_out = not_2_out ? rom_1_data[4:3] : 2'bz;  // Controlled_Buffer controlled_buffer_5
  or or_2 (or_2_out, register_1_q[0], register_1_q[1], register_1_q[2], register_1_q[3], register_1_q[4], register_1_q[5], register_1_q[6], register_1_q[7]);
  or or_3 (or_3_out, register_2_q[0], register_2_q[1], register_2_q[2], register_2_q[3], register_2_q[4], register_2_q[5], register_2_q[6], register_2_q[7]);
  Demultiplexer #(.width(8), .enable("false")) demultiplexer_1 (
    .out0(demultiplexer_1_out0), .out1(demultiplexer_1_out1), .in(banc_de_registre_1_out_7), .sel(or_2_out));
  not not_3 (not_3_out, or_2_out);
  Multiplexer #(.width(8), .enable("false")) multiplexer_2 (
    .in0(\unité_de_calcul_1_out_5 ), .in1(bitselector_2_out), .out(multiplexer_2_out), .sel(decoder_1_out4));
  Register register_1 (
    .D(demultiplexer_1_out0), .en(not_3_out), .Q(register_1_q), .clk(clock_2_out), .clr(clock_1_out));
  Register register_2 (
    .D(demultiplexer_1_out1), .en(nand_1_p2), .Q(register_2_q), .clk(clock_2_out), .clr(clock_1_out));
  // NAND_Gate nand_1: pin names not known; wires that end beside it: or_2_out, nand_1_p2, nand_1_p3
  or or_4 (nand_1_p3, decoder_1_out4, or_3_out);
  Banc_de_registre banc_de_registre_1 (
    .in_3(multiplexer_2_out), .in_4(clock_2_out), .in_5(in_3), .in_6(controlled_buffer_3_out),
    .out_7(banc_de_registre_1_out_7), .activation(in_2), .\opération (in_4));
  \Unité_de_calcul  \unité_de_calcul_1  (
    .A(register_1_q), .E(in_1), .B(register_2_q), .in_4(rom_1_data[1:0]), .out_5(\unité_de_calcul_1_out_5 ));
  // Probe on \unité_de_calcul_1_out_5 
  // Probe on banc_de_registre_1_out_7

  // Notes on the sheet:
  //   contents of rom_1 (hex, n*v repeats v):
  //   c04 e70c 1114 1c1 5b 41 5
endmodule

module \Unité_de_calcul  (
  input  [7:0] A,
  input  E,
  input  [7:0] B,
  input  [1:0] in_4,
  output [7:0] out_5
);

  wire bitselector_1_out, bitselector_2_out, xor_1_out;
  wire [7:0] adder_1_out, controlled_buffer_1_out, controlled_buffer_2_out, divider_1_out, multiplexer_1_out,
       multiplexer_2_out, multiplexer_3_out, multiplexer_4_out, multiplexer_5_out, multiplier_1_out,
       negator_1_out, negator_2_out, negator_3_out, negator_4_out, negator_5_out, negator_6_out,
       subtractor_1_out;

  // Probe on A
  // Probe on B
  assign controlled_buffer_1_out = E ? A : 8'bz;  // Controlled_Buffer controlled_buffer_1
  assign controlled_buffer_2_out = E ? B : 8'bz;  // Controlled_Buffer controlled_buffer_2
  BitSelector bitselector_1 (.in(controlled_buffer_1_out), .out(bitselector_1_out), .sel(3'b111));
  BitSelector bitselector_2 (.in(controlled_buffer_2_out), .out(bitselector_2_out), .sel(3'b111));
  Negator negator_1 (.in(controlled_buffer_1_out), .out(negator_1_out));
  Negator negator_2 (.in(controlled_buffer_2_out), .out(negator_2_out));
  Negator negator_3 (.in(controlled_buffer_1_out), .out(negator_3_out));
  Negator negator_4 (.in(controlled_buffer_2_out), .out(negator_4_out));
  Multiplexer #(.width(8)) multiplexer_1 (
    .in0(controlled_buffer_1_out), .in1(negator_1_out), .out(multiplexer_1_out), .sel(bitselector_1_out));  // open: en
  Multiplexer #(.width(8)) multiplexer_2 (
    .in0(controlled_buffer_2_out), .in1(negator_2_out), .out(multiplexer_2_out), .sel(bitselector_2_out));  // open: en
  Multiplexer #(.width(8)) multiplexer_3 (
    .in0(controlled_buffer_1_out), .in1(negator_3_out), .out(multiplexer_3_out), .sel(bitselector_1_out));  // open: en
  Multiplexer #(.width(8)) multiplexer_4 (
    .in0(controlled_buffer_2_out), .in1(negator_4_out), .out(multiplexer_4_out), .sel(bitselector_2_out));  // open: en
  Adder adder_1 (.a(controlled_buffer_1_out), .b(controlled_buffer_2_out), .out(adder_1_out));  // open: cin, cout
  Subtractor subtractor_1 (
    .a(controlled_buffer_1_out), .b(controlled_buffer_2_out), .out(subtractor_1_out));  // open: bin, bout
  xor xor_1 (xor_1_out, bitselector_1_out, bitselector_2_out);
  Multiplier multiplier_1 (.a(multiplexer_1_out), .b(multiplexer_2_out), .out(multiplier_1_out));  // open: cin, cout
  Divider divider_1 (.a(multiplexer_3_out), .b(multiplexer_4_out), .out(divider_1_out));  // open: upper, rem
  Negator negator_5 (.in(multiplier_1_out), .out(negator_5_out));
  Negator negator_6 (.in(divider_1_out), .out(negator_6_out));
  // Probe on adder_1_out
  Multiplexer #(.width(8), .disabled(0)) multiplexer_5 (
    .in0(multiplier_1_out), .in1(negator_5_out), .out(multiplexer_5_out), .en(xor_1_out));  // open: sel
  Multiplexer #(.width(8)) multiplexer_6 (
    .in0(divider_1_out), .in1(negator_6_out), .out(multiplexer_5_out), .en(xor_1_out));  // open: sel
  // Probe on multiplexer_5_out
  // Probe on multiplexer_5_out
  // Probe on subtractor_1_out
  Multiplexer #(.select(2), .width(8)) multiplexer_7 (
    .in0(adder_1_out), .in1(subtractor_1_out), .in2(multiplexer_5_out), .in3(multiplexer_5_out), .out(out_5),
    .sel(in_4));  // open: en
endmodule

module Banc_de_registre (
  input  activation,
  input  \opération ,
  input  [7:0] in_3,
  input  in_4,
  input  in_5,
  input  [1:0] in_6,
  output [7:0] out_7
);

  wire and_1_out, and_2_out, and_3_out, and_4_out, decoder_1_out0, decoder_1_out1, decoder_1_out2,
       decoder_1_out3;
  wire [7:0] multiplexer_1_out, multiplexer_2_out, multiplexer_3_out, multiplexer_4_out, register_1_q,
       register_2_q, register_3_q, register_4_q;

  // Probe on in_3
  Multiplexer #(.width(8)) multiplexer_1 (
    .in0(register_1_q), .in1(in_3), .out(multiplexer_1_out), .sel(and_1_out));  // open: en
  and and_1 (and_1_out, activation, \opération , decoder_1_out0);
  Decoder #(.select(2)) decoder_1 (
    .out0(decoder_1_out0), .out1(decoder_1_out1), .out2(decoder_1_out2), .out3(decoder_1_out3), .sel(in_6),
    .en(in_5));
  // Probe on register_1_q
  Register register_1 (.D(multiplexer_1_out), .Q(register_1_q), .clk(in_4));  // open: en, clr
  // Probe on register_2_q
  Multiplexer #(.width(8)) multiplexer_2 (
    .in0(register_2_q), .in1(in_3), .out(multiplexer_2_out), .sel(and_2_out));  // open: en
  Register register_2 (.D(multiplexer_2_out), .Q(register_2_q), .clk(in_4));  // open: en, clr
  and and_2 (and_2_out, activation, \opération , decoder_1_out1);
  and and_3 (and_3_out, activation, \opération , decoder_1_out2);
  // Probe on register_3_q
  Multiplexer #(.width(8)) multiplexer_3 (
    .in0(register_3_q), .in1(in_3), .out(multiplexer_3_out), .sel(and_3_out));  // open: en
  Register register_3 (.D(multiplexer_3_out), .Q(register_3_q), .clk(in_4));  // open: en, clr
  Multiplexer #(.width(8)) multiplexer_4 (
    .in0(register_4_q), .in1(in_3), .out(multiplexer_4_out), .sel(and_4_out));  // open: en
  and and_4 (and_4_out, activation, \opération , decoder_1_out3);
  // Probe on register_4_q
  Register register_4 (.D(multiplexer_4_out), .Q(register_4_q), .clk(in_4));  // open: en, clr
  Multiplexer #(.select(2), .width(8)) multiplexer_5 (
    .in0(register_1_q), .in1(register_2_q), .in2(register_3_q), .in3(register_4_q), .out(out_7), .sel(in_6),
    .en(1'b1));
  // Probe on out_7
endmodule
